# Fritzing sketch soilSensor (saved by Fritzing 0.9.4)
circuit board: 2.62645cm x 13.3639cm
breadboards: 1

parts:
  RFM95W = RFM9xW
  R1 = Resistor [tolerance=±1% resistance=3M package="0805 [SMD]"]
  R2 = Resistor [tolerance=±1% resistance=1M package="0805 [SMD]"]
  Mini_Pro = Arduino Pro Mini (3.3V)
  ANTENNA = Antenna
  U1 = MPC1700 [package=sot23-3]
  3V = Battery
  C1 = Ceramic Capacitor [capacitance=1µF package="0805 [SMD, multilayer]"]
  J3 = Soil Sensor PCB [form="♀ (female)"]
  D1 = Rectifier Diode [package="Melf DO-213 AA [SMD]"]
  R3 = Resistor [tolerance=±5% resistance=220 package="0805 [SMD]"]
  C2 = Ceramic Capacitor [capacitance=100nF package="0805 [SMD, multilayer]"]
  R4 = Resistor [tolerance=±5% resistance=220 package="0805 [SMD]"]

nets:
  MISO: RFM95W.MISO, Mini_Pro.MISO
  MOSI: RFM95W.MOSI, Mini_Pro.MOSI
  SCK: RFM95W.SCK, Mini_Pro.SCK
  nss: RFM95W.NSS, Mini_Pro.D6
  nrst: RFM95W.RESET, Mini_Pro.D5
  N1: RFM95W.ANT, ANTENNA.antenna_lead
  GND: RFM95W.GND#9, R2.Pin_0, Mini_Pro.GND, U1.GND, 3V.-, C1.0
  3V: RFM95W.VCC, R1.Pin_1, Mini_Pro.VCC, U1.OUT, C1.1
  dio0: RFM95W.DIO0, Mini_Pro.D2
  dio1: RFM95W.DIO1, Mini_Pro.D3
  dio2: RFM95W.DIO2, Mini_Pro.D4
  BAT_SENSOR: R1.Pin_0, R2.Pin_1, Mini_Pro.A0
  enable sensor: Mini_Pro.A2, R3.Pin_0
  Soil Sensor: Mini_Pro.A1, D1.cathode, C2.1, R4.Pin_1
  N2: U1.IN, 3V.+
  N3: J3.GND, C2.0, R4.Pin_0
  N4: J3.Sig, D1.anode, R3.Pin_1

notes:
  SIG
  +
  IN
  Soil Lora
  05/2020
  V0.8

custom parts:
  RFM9xW: RFM9xW Module connector
  MPC1700: Small package LDO
  Soil Sensor PCB: Generic female header
